// Logisim project 01_intro.circ as structural Verilog: 1 circuit, main circuit main
module main (
  input  in_1,
  input  in_2
);

  wire and_1_out, nand_1_out, not_1_out, or_1_out, xnor_1_out, xor_1_out;

  // NOR_Gate nor_1 has open pins: in0=in_1, in1=in_2, out=open
  and and_1 (and_1_out, in_1, in_2);
  not not_1 (not_1_out, in_1);
  or or_1 (or_1_out, in_1, in_2);
  nand nand_1 (nand_1_out, in_1, in_2);
  xor xor_1 (xor_1_out, in_1, in_2);
  LED LED1 (.in(and_1_out));
  LED led_1 (.in(not_1_out));
  LED led_2 (.in(or_1_out));
  LED led_3 (.in(nand_1_out));
  LED led_4 (.in(xor_1_out));
  xnor xnor_1 (xnor_1_out, in_1, in_2);
  LED led_5 (.in(xnor_1_out));
endmodule
