// Logisim project FirstSchematic.circ as structural Verilog: 1 circuit, main circuit main
module main (
);

  wire and_1_out, buffer_1_out, button_1_out, button_2_out, controlled_buffer_1_out,
       controlled_inverter_1_out, dipswitch_1_p1, dipswitch_1_p2, dipswitch_1_p3, dipswitch_1_p4,
       dipswitch_1_p5, dipswitch_1_p6, dipswitch_1_p7, dipswitch_1_p8, dipswitch_2_p1, dipswitch_2_p2,
       dipswitch_2_p3, dipswitch_2_p4, dipswitch_2_p5, dipswitch_2_p6, dipswitch_2_p7, dipswitch_2_p8,
       nand_1_out, nor_1_out, not_1_out, or_1_out, xnor_1_out, xor_1_out;

  // DipSwitch dipswitch_1: pin names not known; wires that end beside it: dipswitch_1_p1, dipswitch_1_p2, dipswitch_1_p3, dipswitch_1_p4, dipswitch_1_p5, dipswitch_1_p6, dipswitch_1_p7, dipswitch_1_p8
  // DipSwitch dipswitch_2: pin names not known; wires that end beside it: dipswitch_2_p1, dipswitch_2_p2, dipswitch_2_p3, dipswitch_2_p4, dipswitch_2_p5, dipswitch_2_p6, dipswitch_2_p7, dipswitch_2_p8
  Button button_1 (.out(button_1_out));
  Button button_2 (.out(button_2_out));
  not not_1 (not_1_out, button_1_out);
  buf buffer_1 (buffer_1_out, button_2_out);
  assign controlled_buffer_1_out = dipswitch_2_p6 ? dipswitch_2_p5 : 1'bz;  // Controlled_Buffer controlled_buffer_1
  assign controlled_inverter_1_out = dipswitch_2_p8 ? ~dipswitch_2_p7 : 1'bz;  // Controlled_Inverter controlled_inverter_1
  LED led_1 (.in(not_1_out));
  LED led_2 (.in(buffer_1_out));
  and and_1 (and_1_out, dipswitch_1_p1, dipswitch_1_p2);
  or or_1 (or_1_out, dipswitch_1_p3, dipswitch_1_p4);
  nand nand_1 (nand_1_out, dipswitch_1_p5, dipswitch_1_p6);
  nor nor_1 (nor_1_out, dipswitch_1_p7, dipswitch_1_p8);
  xor xor_1 (xor_1_out, dipswitch_2_p1, dipswitch_2_p2);
  xnor xnor_1 (xnor_1_out, dipswitch_2_p3, dipswitch_2_p4);
  LedBar ledbar_1 (
    .led0(and_1_out), .led1(or_1_out), .led2(nand_1_out), .led3(nor_1_out), .led4(xor_1_out),
    .led5(xnor_1_out), .led6(controlled_buffer_1_out), .led7(controlled_inverter_1_out));
endmodule
