// Logisim project 5.circ as structural Verilog: 1 circuit, main circuit main
module main (
  input  IN1,
  input  IN2,
  input  IN3,
  input  IN4,
  input  IN5,
  input  IN6,
  input  IN7,
  input  IN8,
  input  IN9,
  output OUT1,
  output OUT2,
  output OUT3,
  output OUT4
);

  wire U1_out, U2_out, U3_out, U4_out, U5_out, U6_out, U7_out, U8_out, U9_out, U10_out, U11_out, U12_out,
       U16_out;

  nor U16 (U16_out, IN8, IN9);
  and U1 (U1_out, IN1, ~IN2, ~IN4, ~IN6, U16_out);  // AND_Gate
  and U2 (U2_out, IN3, ~IN4, ~IN6, U16_out);  // AND_Gate
  and U3 (U3_out, IN5, ~IN6, U16_out);  // AND_Gate
  and U4 (U4_out, IN7, U16_out);
  and U5 (U5_out, IN2, ~IN4, ~IN5, U16_out);  // AND_Gate
  and U6 (U6_out, ~IN4, ~IN5, IN3, U16_out);  // AND_Gate
  and U7 (U7_out, IN6, U16_out);
  and U8 (U8_out, IN7, U16_out);
  and U9 (U9_out, IN4, U16_out);
  and U10 (U10_out, IN5, U16_out);
  and U11 (U11_out, IN6, U16_out);
  and U12 (U12_out, IN7, U16_out);
  or U17 (OUT4, IN9, IN8);
  or U13 (OUT1, U1_out, U2_out, U3_out, U4_out, IN9);
  or U14 (OUT2, U5_out, U6_out, U7_out, U8_out);
  or U15 (OUT3, U9_out, U10_out, U11_out, U12_out);
  Hex_Digit_Display hex_digit_display_1 (.value({OUT4, OUT3, OUT2, OUT1}));  // open: dp
endmodule
