// Logisim project FiveMemory.circ as structural Verilog: 1 circuit, main circuit main
module main (
  input  Dx1,
  input  Ex1,
  input  Rx1,
  input  Sx1,
  input  Sx12,
  input  Ex12,
  input  Rx12,
  input  [1:0] CX12,
  input  [1:0] DX12,
  output x1Q,
  output x1Q2,
  output Qx1,
  output Qx12,
  output x1Q12,
  output x1Q13,
  output [1:0] x1Q21,
  output [1:0] x1Q22
);

  wire DATA_out, ON1_out, ON2_out, ONOFF_out;
  wire [1:0] S1_out, S2_out, S3_out, S4_out;

  nand ON1 (ON1_out, Sx12, Ex12);
  nand ON2 (ON2_out, Ex12, Rx12);
  nand DATA (DATA_out, Dx1, Ex1);
  nand ONOFF (ONOFF_out, DATA_out, Ex1);
  nor WORK1 (Qx1, Rx1, Qx12);
  nor WORK2 (Qx12, Qx1, Sx1);
  assign S1_out = ~(S4_out & S2_out);  // NAND_Gate S1, 2 bits wide
  assign S2_out = ~(S1_out & CX12);  // NAND_Gate S2, 2 bits wide
  assign S3_out = ~(S2_out & CX12 & S4_out);  // NAND_Gate S3, 2 bits wide
  assign S4_out = ~(S3_out & DX12);  // NAND_Gate S4, 2 bits wide
  not CELL12 (x1Q12, ON1_out);  // NAND_Gate
  not CELL21 (x1Q13, ON2_out);  // NAND_Gate
  nand CELL1 (x1Q, DATA_out, x1Q2);
  nand CELL2 (x1Q2, x1Q, ONOFF_out);
  assign x1Q21 = ~(S2_out & x1Q22);  // NAND_Gate CELL13, 2 bits wide
  assign x1Q22 = ~(x1Q21 & S3_out);  // NAND_Gate CELL23, 2 bits wide

  // Notes on the sheet:
  //   Data pin
  //   On/off switch
  //   On/off and Transfer data
  //   Transfer data and on/off
  //   On/off switch
  //   D-trigger
  //   1
  //   RS-trigger (async)
  //   RS-trigger (Switch-mode)
  //   RS-trigger part
  //   D-trigger (Sync)
  //   Output data
  //   Independent value
endmodule
