// Logisim project FourthEncoder.circ as structural Verilog: 1 circuit, main circuit main
module main (
  input  In1,
  input  In2,
  input  In3,
  input  In4,
  input  In5,
  input  In6,
  input  In7,
  input  In8,
  input  In9,
  output Out1,
  output Out2,
  output Out3,
  output Out4
);

  wire U1_out, U2_out, U3_out, U4_out, U5_out, U6_out, U7_out, U8_out, U9_out, U10_out, U11_out, U12_out,
       U16_out;

  // DipSwitch #(.number(9)) dipswitch_1: pin names not known; wires that end beside it: In1, In2, In3, In4, In5, In6, In7, In8, In9
  nor U16 (U16_out, In8, In9);
  and U1 (U1_out, In1, ~In2, ~In4, ~In6, U16_out);  // AND_Gate
  and U2 (U2_out, In3, ~In4, ~In6, U16_out);  // AND_Gate
  and U3 (U3_out, In5, ~In6, U16_out);  // AND_Gate
  and U4 (U4_out, In7, U16_out);
  and U5 (U5_out, In2, ~In4, ~In5, U16_out);  // AND_Gate
  and U6 (U6_out, ~In4, ~In5, In3, U16_out);  // AND_Gate
  and U7 (U7_out, In6, U16_out);
  and U8 (U8_out, In7, U16_out);
  and U9 (U9_out, In4, U16_out);
  and U10 (U10_out, In5, U16_out);
  and U11 (U11_out, In6, U16_out);
  and U12 (U12_out, In7, U16_out);
  or U13 (Out1, U1_out, U2_out, U3_out, U4_out, In9);
  or U14 (Out2, U5_out, U6_out, U7_out, U8_out);
  or U15 (Out3, U9_out, U10_out, U11_out, U12_out);
  or U17 (Out4, In9, In8);
  Hex_Digit_Display #(.decimalPoint("false")) hex_digit_display_1 (.value({Out4, Out3, Out2, Out1}));
endmodule
