// Logisim project Lab10_RAM.circ as structural Verilog: 1 circuit, main circuit main
module main (
);

  wire and_1_out, and_2_out, clk, clr_out, rd, rd_wrt_out, Reset_out, wrt;
  wire [6:0] controlled_buffer_2_out, keyboard_1_data;
  wire [7:0] counter_1_q, ram_1_data;
  wire [7:7] controlled_buffer_2_out_2;

  Button u_clk (.out(clk));
  Button Reset (.out(Reset_out));
  Counter counter_1 (.clr(Reset_out), .clk(clk), .Q(counter_1_q));  // open: load, up, count, D, carry
  T_Flip_Flop t_ff_1 (.T(1'b1), .clk(rd_wrt_out), .Q(wrt), .Qn(rd));  // open: reset, preset
  Button rd_wrt (.out(rd_wrt_out));
  RAM #(.databus("bidir")) ram_1 (.addr(counter_1_q), .we(wrt), .oe(rd), .clk(clk), .data(ram_1_data));
  LED led_1 (.in(wrt));
  and and_1 (and_1_out, clk, wrt);
  Keyboard keyboard_1 (.clk(and_1_out), .data(keyboard_1_data));  // open: re, clr, avail
  LED led_2 (.in(rd));
  and and_2 (and_2_out, clk, wrt);
  assign ram_1_data = wrt ? {1'b0, keyboard_1_data} : 8'bz;  // Controlled_Buffer controlled_buffer_1
  assign {controlled_buffer_2_out_2[7], controlled_buffer_2_out} = rd ? ram_1_data : 8'bz;  // Controlled_Buffer controlled_buffer_2
  TTY tty_1 (.data(controlled_buffer_2_out), .clk(and_2_out), .clr(clr_out));  // open: we
  Button clr (.out(clr_out));

  // Notes on the sheet:
  //   Name
  //   Lab 10: RAM
  //   Date
endmodule
