// Logisim project LogisimtoSystemVerilog.circ as structural Verilog: 1 circuit, main circuit main
module main (
  input  a,
  input  sel,
  input  b,
  output F3
);

  wire AND1_out, AND2_out, NOT1_out;

  not NOT1 (NOT1_out, sel);
  and AND1 (AND1_out, a, NOT1_out);
  and AND2 (AND2_out, sel, b);
  or OR1 (F3, AND1_out, AND2_out);

  // Notes on the sheet:
  //   endmodule mux
  //   a x n_sel + b x sel
  //   module mux (output logic F3, input logic a, sel, b);
  //   G1
  //   A
  //   NEGATIVE_SEL
  //   SEL
  //   B
  //   G2
  //   Функция G1 (and#2) -> G1 (F1, A, NEGATIVE_SEL)
  //   F1
  //   G3
  //   F2
  //   Функция G2 (and#1) -> G2 (F2, B, SEL)
  //   Функция G3 (or#1) -> G3 (F3, F2, F1)
endmodule
