// Logisim project SecondMultiplexer.circ as structural Verilog: 1 circuit, main circuit main
module main (
  input  Sel,
  input  In1,
  input  In2,
  input  In11,
  input  In21,
  input  Sel2,
  output Out1,
  output Out11
);

  wire and_1_out, and_2_out, not_1_out, not_2_out;

  not not_1 (not_1_out, Sel);
  not not_2 (not_2_out, not_1_out);
  and and_1 (and_1_out, not_2_out, In1);
  and and_2 (and_2_out, not_1_out, In2);
  Multiplexer multiplexer_1 (.in0(In11), .in1(In21), .out(Out11), .sel(Sel2));
  or or_1 (Out1, and_1_out, and_2_out);
endmodule
