// Logisim project SixthDtrigger.circ as structural Verilog: 1 circuit, main circuit main
module main (
  input  Clock,
  input  [8:0] in_2
);

  wire BANK1_sw1, BANK1_sw2, BANK1_sw3, BANK1_sw4, BANK1_sw5, BANK1_sw6, BANK1_sw7, BANK1_sw8, BANK1_sw9,
       BANK2_sw1, BANK2_sw2, BANK2_sw3, BANK2_sw4, BANK2_sw5, BANK2_sw6, BANK2_sw7, BANK2_sw8, BANK2_sw9,
       BANK3_sw1, BANK3_sw2, BANK3_sw3, BANK3_sw4, BANK3_sw5, BANK3_sw6, BANK3_sw7, BANK3_sw8, BANK3_sw9,
       C11_q, C12_q, C13_q, C14_q, C15_q, C16_q, C17_q, C18_q, C21_q, C22_q, C23_q, C24_q, C25_q, C26_q,
       C27_q, C28_q, C29_q, C31_q, C32_q, C34_q, C35_q, C36_q, C37_q, C38_q, C39_q, C41_q, C42_q, C43_q,
       C44_q, C45_q, C46_q, C47_q, C48_q, d_ff_1_q, d_ff_2_q, ENABLE_sw1, ENABLE_sw2, ENABLE_sw3, ENABLE_sw4,
       RESET_sw1, RESET_sw2, RESET_sw3, RESET_sw4;

  D_Flip_Flop #(.trigger("low")) C11 (
    .clk(Clock), .D(in_2[0]), .Q(C11_q), .preset(ENABLE_sw1), .reset(RESET_sw1));  // open: Qn
  D_Flip_Flop #(.trigger("low")) C12 (
    .clk(Clock), .D(in_2[1]), .Q(C12_q), .preset(ENABLE_sw1), .reset(RESET_sw1));  // open: Qn
  D_Flip_Flop #(.trigger("low")) C13 (
    .clk(Clock), .D(in_2[2]), .Q(C13_q), .preset(ENABLE_sw1), .reset(RESET_sw1));  // open: Qn
  D_Flip_Flop #(.trigger("low")) C14 (
    .clk(Clock), .D(in_2[3]), .Q(C14_q), .preset(ENABLE_sw1), .reset(RESET_sw1));  // open: Qn
  D_Flip_Flop #(.trigger("low")) C15 (
    .clk(Clock), .D(in_2[4]), .Q(C15_q), .preset(ENABLE_sw1), .reset(RESET_sw1));  // open: Qn
  D_Flip_Flop #(.trigger("low")) C16 (
    .clk(Clock), .D(in_2[5]), .Q(C16_q), .preset(ENABLE_sw1), .reset(RESET_sw1));  // open: Qn
  D_Flip_Flop #(.trigger("low")) C17 (
    .clk(Clock), .D(in_2[6]), .Q(C17_q), .preset(ENABLE_sw1), .reset(RESET_sw1));  // open: Qn
  D_Flip_Flop #(.trigger("low")) C18 (
    .clk(Clock), .D(in_2[7]), .Q(C18_q), .preset(ENABLE_sw1), .reset(RESET_sw1));  // open: Qn
  D_Flip_Flop #(.trigger("low")) C19 (.clk(Clock), .D(in_2[8]), .preset(ENABLE_sw1), .reset(RESET_sw1));  // open: Q, Qn
  DipSwitch #(.number(4)) ENABLE (.sw1(ENABLE_sw1), .sw2(ENABLE_sw2), .sw3(ENABLE_sw3), .sw4(ENABLE_sw4));
  _7_Segment_Display u_7_segment_display_1 (
    .g(C14_q), .f(C15_q), .a(C16_q), .b(C17_q), .e(C11_q), .d(C12_q), .c(C13_q), .dp(C18_q));
  DipSwitch #(.number(9)) BANK1 (
    .sw1(BANK1_sw1), .sw2(BANK1_sw2), .sw3(BANK1_sw3), .sw4(BANK1_sw4), .sw5(BANK1_sw5), .sw6(BANK1_sw6),
    .sw7(BANK1_sw7), .sw8(BANK1_sw8), .sw9(BANK1_sw9));
  DipSwitch #(.number(4)) RESET (.sw1(RESET_sw1), .sw2(RESET_sw2), .sw3(RESET_sw3), .sw4(RESET_sw4));
  D_Flip_Flop #(.trigger("low")) C21 (
    .clk(Clock), .D(BANK1_sw1), .Q(C21_q), .preset(ENABLE_sw2), .reset(RESET_sw2));  // open: Qn
  D_Flip_Flop #(.trigger("low")) C22 (
    .clk(Clock), .D(BANK1_sw2), .Q(C22_q), .preset(ENABLE_sw2), .reset(RESET_sw2));  // open: Qn
  D_Flip_Flop #(.trigger("low")) C23 (
    .clk(Clock), .D(BANK1_sw3), .Q(C23_q), .preset(ENABLE_sw2), .reset(RESET_sw2));  // open: Qn
  D_Flip_Flop #(.trigger("low")) C24 (
    .clk(Clock), .D(BANK1_sw4), .Q(C24_q), .preset(ENABLE_sw2), .reset(RESET_sw2));  // open: Qn
  D_Flip_Flop #(.trigger("low")) C25 (
    .clk(Clock), .D(BANK1_sw5), .Q(C25_q), .preset(ENABLE_sw2), .reset(RESET_sw2));  // open: Qn
  D_Flip_Flop #(.trigger("low")) C26 (
    .clk(Clock), .D(BANK1_sw6), .Q(C26_q), .preset(ENABLE_sw2), .reset(RESET_sw2));  // open: Qn
  D_Flip_Flop #(.trigger("low")) C27 (
    .clk(Clock), .D(BANK1_sw7), .Q(C27_q), .preset(ENABLE_sw2), .reset(RESET_sw2));  // open: Qn
  D_Flip_Flop #(.trigger("low")) C28 (
    .clk(Clock), .D(BANK1_sw8), .Q(C28_q), .preset(ENABLE_sw2), .reset(RESET_sw2));  // open: Qn
  D_Flip_Flop #(.trigger("low")) C29 (
    .clk(Clock), .D(BANK1_sw9), .Q(C29_q), .preset(ENABLE_sw2), .reset(RESET_sw2));  // open: Qn
  DipSwitch #(.number(9)) BANK2 (
    .sw1(BANK2_sw1), .sw2(BANK2_sw2), .sw3(BANK2_sw3), .sw4(BANK2_sw4), .sw5(BANK2_sw5), .sw6(BANK2_sw6),
    .sw7(BANK2_sw7), .sw8(BANK2_sw8), .sw9(BANK2_sw9));
  D_Flip_Flop #(.trigger("low")) C31 (
    .clk(Clock), .D(BANK2_sw1), .Q(C31_q), .preset(ENABLE_sw3), .reset(RESET_sw3));  // open: Qn
  D_Flip_Flop #(.trigger("low")) C32 (
    .clk(Clock), .D(BANK2_sw2), .Q(C32_q), .preset(ENABLE_sw3), .reset(RESET_sw3));  // open: Qn
  D_Flip_Flop #(.trigger("low")) C34 (
    .clk(Clock), .D(BANK2_sw3), .Q(C34_q), .preset(ENABLE_sw3), .reset(RESET_sw3));  // open: Qn
  D_Flip_Flop #(.trigger("low")) C35 (
    .clk(Clock), .D(BANK2_sw4), .Q(C35_q), .preset(ENABLE_sw3), .reset(RESET_sw3));  // open: Qn
  D_Flip_Flop #(.trigger("low")) C36 (
    .clk(Clock), .D(BANK2_sw5), .Q(C36_q), .preset(ENABLE_sw3), .reset(RESET_sw3));  // open: Qn
  D_Flip_Flop #(.trigger("low")) C37 (
    .clk(Clock), .D(BANK2_sw6), .Q(C37_q), .preset(ENABLE_sw3), .reset(RESET_sw3));  // open: Qn
  D_Flip_Flop #(.trigger("low")) C38 (
    .clk(Clock), .D(BANK2_sw7), .Q(C38_q), .preset(ENABLE_sw3), .reset(RESET_sw3));  // open: Qn
  D_Flip_Flop #(.trigger("low")) C39 (
    .clk(Clock), .D(BANK2_sw8), .Q(C39_q), .preset(ENABLE_sw3), .reset(RESET_sw3));  // open: Qn
  D_Flip_Flop #(.trigger("low")) d_ff_1 (
    .clk(Clock), .D(BANK2_sw9), .Q(d_ff_1_q), .preset(ENABLE_sw3), .reset(RESET_sw3));  // open: Qn
  DipSwitch #(.number(9)) BANK3 (
    .sw1(BANK3_sw1), .sw2(BANK3_sw2), .sw3(BANK3_sw3), .sw4(BANK3_sw4), .sw5(BANK3_sw5), .sw6(BANK3_sw6),
    .sw7(BANK3_sw7), .sw8(BANK3_sw8), .sw9(BANK3_sw9));
  D_Flip_Flop #(.trigger("low")) C41 (
    .clk(Clock), .D(BANK3_sw1), .Q(C41_q), .preset(ENABLE_sw4), .reset(RESET_sw4));  // open: Qn
  D_Flip_Flop #(.trigger("low")) C42 (
    .clk(Clock), .D(BANK3_sw2), .Q(C42_q), .preset(ENABLE_sw4), .reset(RESET_sw4));  // open: Qn
  D_Flip_Flop #(.trigger("low")) C43 (
    .clk(Clock), .D(BANK3_sw3), .Q(C43_q), .preset(ENABLE_sw4), .reset(RESET_sw4));  // open: Qn
  D_Flip_Flop #(.trigger("low")) C44 (
    .clk(Clock), .D(BANK3_sw4), .Q(C44_q), .preset(ENABLE_sw4), .reset(RESET_sw4));  // open: Qn
  D_Flip_Flop #(.trigger("low")) C45 (
    .clk(Clock), .D(BANK3_sw5), .Q(C45_q), .preset(ENABLE_sw4), .reset(RESET_sw4));  // open: Qn
  D_Flip_Flop #(.trigger("low")) C46 (
    .clk(Clock), .D(BANK3_sw6), .Q(C46_q), .preset(ENABLE_sw4), .reset(RESET_sw4));  // open: Qn
  D_Flip_Flop #(.trigger("low")) C47 (
    .clk(Clock), .D(BANK3_sw7), .Q(C47_q), .preset(ENABLE_sw4), .reset(RESET_sw4));  // open: Qn
  D_Flip_Flop #(.trigger("low")) C48 (
    .clk(Clock), .D(BANK3_sw8), .Q(C48_q), .preset(ENABLE_sw4), .reset(RESET_sw4));  // open: Qn
  D_Flip_Flop #(.trigger("low")) d_ff_2 (
    .clk(Clock), .D(BANK3_sw9), .Q(d_ff_2_q), .preset(ENABLE_sw4), .reset(RESET_sw4));  // open: Qn
endmodule
