// Logisim project ThridEquation.circ as structural Verilog: 1 circuit, main circuit main
module main (
  input  In1A,
  input  In1B,
  input  In1C,
  output Out1
);

  wire AND1_out, AND2_out, AND3_out;

  and AND1 (AND1_out, ~In1A, In1B, ~In1C);  // AND_Gate
  and AND2 (AND2_out, In1A, ~In1B, ~In1C);  // AND_Gate
  and AND3 (AND3_out, In1A, In1B, In1C);
  or OR1 (Out1, AND1_out, AND2_out, AND3_out);
endmodule
